// Logisim project Circuitos.circ as structural Verilog: 8 circuits, main circuit Sumas
module Sumas (
  input  [3:0] in_1,
  input  [3:0] in_2,
  input  [3:0] in_3
);

  wire [3:0] sumar_3_1_u, sumar_4_1_u, sumar_8_1_u;

  Sumar_4 sumar_4_1 (
    .a(in_1[3]), .b(in_1[2]), .c(in_1[1]), .d(in_1[0]), .x(sumar_4_1_u[3]), .y(sumar_4_1_u[2]),
    .z(sumar_4_1_u[1]), .u(sumar_4_1_u[0]));
  Sumar_8 sumar_8_1 (
    .a(in_2[3]), .b(in_2[2]), .c(in_2[1]), .d(in_2[0]), .x(sumar_8_1_u[3]), .y(sumar_8_1_u[2]),
    .z(sumar_8_1_u[1]), .u(sumar_8_1_u[0]));
  Sumar_3 sumar_3_1 (
    .a(in_3[3]), .b(in_3[2]), .c(in_3[1]), .d(in_3[0]), .x(sumar_3_1_u[3]), .y(sumar_3_1_u[2]),
    .z(sumar_3_1_u[1]), .u(sumar_3_1_u[0]));
  Hex_Digit_Display hex_digit_display_1 (.value(sumar_4_1_u));  // open: dp
  Hex_Digit_Display hex_digit_display_2 (.value(sumar_8_1_u));  // open: dp
  Hex_Digit_Display hex_digit_display_3 (.value(sumar_3_1_u));  // open: dp

  // Notes on the sheet:
  //   "Circuito Sumar 4"
  //   "Circuito Sumar 8"
  //   "Circuito Sumar 3"
endmodule

module Sumar_4 (
  input  a,
  input  b,
  input  c,
  input  d,
  output x,
  output y,
  output z,
  output u
);

  wire and_1_out, and_2_out, not_1_out, not_2_out;

  not not_1 (not_1_out, a);
  and and_1 (and_1_out, not_1_out, b);
  and and_2 (and_2_out, a, not_2_out);
  not not_2 (not_2_out, b);
  not not_3 (y, b);
  or or_1 (x, and_1_out, and_2_out);

  assign u = d;
  assign z = c;
endmodule

module Sumar_8 (
  input  a,
  input  b,
  input  c,
  input  d,
  output x,
  output y,
  output z,
  output u
);

  not not_1 (x, a);

  assign u = d;
  assign y = b;
  assign z = c;
endmodule

module Sumar_3 (
  input  a,
  input  b,
  input  c,
  input  d,
  output x,
  output y,
  output z,
  output u
);

  wire and_1_out, and_2_out, and_3_out, and_4_out, and_5_out, and_6_out, and_7_out, and_8_out, and_9_out,
       not_1_out, not_2_out, not_3_out, not_4_out, not_5_out, not_6_out, not_7_out, not_8_out, not_9_out,
       not_10_out, not_11_out;

  not not_1 (not_1_out, a);
  and and_1 (and_1_out, not_1_out, b, d);
  not not_2 (not_2_out, a);
  and and_2 (and_2_out, not_2_out, b, c);
  and and_3 (and_3_out, a, not_3_out);
  not not_3 (not_3_out, b);
  and and_4 (and_4_out, a, not_4_out, not_5_out);
  not not_4 (not_4_out, c);
  not not_5 (not_5_out, d);
  not not_6 (not_6_out, b);
  and and_5 (and_5_out, not_6_out, d);
  not not_7 (not_7_out, b);
  and and_6 (and_6_out, not_7_out, c);
  not not_8 (not_8_out, c);
  and and_7 (and_7_out, b, not_8_out, not_9_out);
  not not_9 (not_9_out, d);
  not not_10 (not_10_out, c);
  and and_8 (and_8_out, not_10_out, not_11_out);
  not not_11 (not_11_out, d);
  and and_9 (and_9_out, c, d);
  not not_12 (u, d);
  or or_1 (x, and_1_out, and_2_out, and_3_out, and_4_out);
  or or_2 (y, and_5_out, and_6_out, and_7_out);
  or or_3 (z, and_8_out, and_9_out);
endmodule

module Restar_3 (
  input  a,
  input  b,
  input  c,
  input  d,
  output x,
  output y,
  output z,
  output u
);

  wire and_1_out, and_2_out, and_3_out, and_4_out, and_5_out, and_6_out, and_7_out, and_8_out, and_9_out,
       not_1_out, not_2_out, not_3_out, not_4_out, not_5_out, not_6_out, not_7_out, not_8_out, not_9_out,
       not_10_out, not_11_out, not_12_out;

  not not_1 (not_1_out, a);
  not not_2 (not_2_out, b);
  and and_1 (and_1_out, not_1_out, not_2_out, not_3_out);
  not not_3 (not_3_out, c);
  not not_4 (not_4_out, a);
  and and_2 (and_2_out, not_4_out, not_5_out, not_6_out);
  not not_5 (not_5_out, b);
  not not_6 (not_6_out, d);
  and and_3 (and_3_out, a, c, d);
  and and_4 (and_4_out, a, b);
  not not_7 (not_7_out, b);
  and and_5 (and_5_out, not_7_out, not_8_out);
  not not_8 (not_8_out, c);
  not not_9 (not_9_out, b);
  and and_6 (and_6_out, not_9_out, not_10_out);
  not not_10 (not_10_out, d);
  and and_7 (and_7_out, b, c, d);
  not not_11 (not_11_out, c);
  and and_8 (and_8_out, not_11_out, d);
  and and_9 (and_9_out, c, not_12_out);
  not not_12 (not_12_out, d);
  not not_13 (u, d);
  or or_1 (x, and_1_out, and_2_out, and_3_out, and_4_out);
  or or_2 (y, and_5_out, and_6_out, and_7_out);
  or or_3 (z, and_8_out, and_9_out);
endmodule

module Restar_4 (
  input  a,
  input  b,
  input  c,
  input  d,
  output x,
  output y,
  output z,
  output u
);

  wire and_1_out, and_2_out, not_1_out, not_2_out;

  not not_1 (not_1_out, a);
  and and_1 (and_1_out, not_1_out, not_2_out);
  not not_2 (not_2_out, b);
  and and_2 (and_2_out, a, b);
  not not_3 (y, b);
  or or_1 (x, and_1_out, and_2_out);

  assign u = d;
  assign z = c;
endmodule

module Restar_8 (
  input  a,
  input  b,
  input  c,
  input  d,
  output x,
  output y,
  output z,
  output u
);

  not not_1 (x, a);

  assign u = d;
  assign y = b;
  assign z = c;
endmodule

module Restas (
  input  [3:0] in_1,
  input  [3:0] in_2,
  input  [3:0] in_3
);

  wire [3:0] restar_3_1_u, restar_4_1_u, restar_8_1_u;

  Restar_4 restar_4_1 (
    .a(in_1[3]), .b(in_1[2]), .c(in_1[1]), .d(in_1[0]), .x(restar_4_1_u[3]), .y(restar_4_1_u[2]),
    .z(restar_4_1_u[1]), .u(restar_4_1_u[0]));
  Restar_8 restar_8_1 (
    .a(in_2[3]), .b(in_2[2]), .c(in_2[1]), .d(in_2[0]), .x(restar_8_1_u[3]), .y(restar_8_1_u[2]),
    .z(restar_8_1_u[1]), .u(restar_8_1_u[0]));
  Restar_3 restar_3_1 (
    .a(in_3[3]), .b(in_3[2]), .c(in_3[1]), .d(in_3[0]), .x(restar_3_1_u[3]), .y(restar_3_1_u[2]),
    .z(restar_3_1_u[1]), .u(restar_3_1_u[0]));
  Hex_Digit_Display hex_digit_display_1 (.value(restar_4_1_u));  // open: dp
  Hex_Digit_Display hex_digit_display_2 (.value(restar_8_1_u));  // open: dp
  Hex_Digit_Display hex_digit_display_3 (.value(restar_3_1_u));  // open: dp

  // Notes on the sheet:
  //   "Circuito Restar 4"
  //   "Circuito Restar 8"
  //   "Circuito Restar 3"
endmodule
