// Logisim project Circuitos.circ as structural Verilog: 6 circuits, main circuit Modulo 8
module Modulo_8 (
  input  in_1,
  output out_2,
  output out_3,
  output out_4
);

  wire and_1_out, and_2_out, and_3_out, and_4_out, and_5_out, and_6_out, clock_1_out, d_ff_1_qn, d_ff_2_qn,
       not_1_out, not_2_out, not_3_out, not_4_out, or_1_out, or_2_out;

  not not_1 (not_1_out, in_1);
  not not_2 (not_2_out, out_2);
  Clock clock_1 (.out(clock_1_out));
  and and_1 (and_1_out, out_2, not_1_out, d_ff_2_qn);
  and and_2 (and_2_out, not_1_out, out_3, not_2_out, out_4);
  not not_3 (not_3_out, out_4);
  not not_4 (not_4_out, out_4);
  and and_3 (and_3_out, not_1_out, out_3, out_2, not_3_out);
  and and_4 (and_4_out, not_1_out, d_ff_2_qn, out_4);
  and and_5 (and_5_out, not_1_out, out_3, not_4_out);
  or or_1 (or_1_out, and_1_out, and_2_out, and_3_out);
  or or_2 (or_2_out, and_4_out, and_5_out);
  and and_6 (and_6_out, not_1_out, d_ff_1_qn);
  D_Flip_Flop d_ff_1 (.clk(clock_1_out), .D(and_6_out), .Q(out_4), .Qn(d_ff_1_qn));  // open: preset, en, reset
  D_Flip_Flop d_ff_2 (.clk(clock_1_out), .D(or_2_out), .Q(out_3), .Qn(d_ff_2_qn));  // open: preset, en, reset
  D_Flip_Flop d_ff_3 (.clk(clock_1_out), .D(or_1_out), .Q(out_2));  // open: Qn, preset, en, reset
endmodule

module Modulo_8_In (
  input  a,
  input  b,
  input  c,
  input  d,
  output x,
  output y,
  output z
);

  wire and_1_out, and_2_out, and_3_out, and_4_out, and_5_out, and_6_out, not_1_out, not_2_out, not_3_out,
       not_4_out, not_5_out, not_6_out, not_7_out, not_8_out, not_9_out, not_10_out, not_11_out, not_12_out;

  not not_1 (not_1_out, a);
  and and_1 (and_1_out, not_1_out, b, not_2_out);
  not not_2 (not_2_out, c);
  not not_3 (not_3_out, a);
  and and_2 (and_2_out, not_3_out, b, not_4_out);
  not not_4 (not_4_out, d);
  not not_5 (not_5_out, a);
  and and_3 (and_3_out, not_5_out, not_6_out, c);
  not not_6 (not_6_out, b);
  not not_7 (not_7_out, a);
  and and_4 (and_4_out, not_7_out, c, not_8_out);
  not not_8 (not_8_out, d);
  not not_9 (not_9_out, a);
  not not_10 (not_10_out, b);
  and and_5 (and_5_out, not_9_out, not_10_out, d);
  not not_11 (not_11_out, a);
  and and_6 (and_6_out, not_11_out, not_12_out, d);
  not not_12 (not_12_out, c);
  or or_1 (x, and_1_out, and_2_out);
  or or_2 (y, and_3_out, and_4_out);
  or or_3 (z, and_5_out, and_6_out);
endmodule

module Modulo_8_Out (
  input  a,
  input  b,
  input  c,
  output x,
  output y,
  output z
);


  assign x = a;
  assign y = b;
  assign z = c;
endmodule

module Secuencia (
  input  in_1,
  output out_2
);

  wire and_1_out, and_2_out, and_3_out, and_4_out, and_5_out, clock_1_out, d_ff_2_q, d_ff_2_qn, d_ff_3_q,
       d_ff_3_qn, not_1_out, or_1_out;

  not not_1 (not_1_out, in_1);
  and and_1 (and_1_out, not_1_out, d_ff_2_qn, d_ff_3_q);
  and and_2 (and_2_out, not_1_out, out_2, d_ff_3_q);
  and and_3 (and_3_out, in_1, out_2, d_ff_3_qn);
  and and_4 (and_4_out, in_1, d_ff_2_q, d_ff_3_qn);
  Clock clock_1 (.out(clock_1_out));
  or or_1 (or_1_out, and_1_out, and_2_out, and_3_out, and_4_out);
  and and_5 (and_5_out, d_ff_3_q, d_ff_2_q);
  D_Flip_Flop d_ff_1 (.clk(clock_1_out), .D(and_5_out), .Q(out_2));  // open: Qn, preset, en, reset
  D_Flip_Flop d_ff_2 (.clk(clock_1_out), .D(or_1_out), .Q(d_ff_2_q), .Qn(d_ff_2_qn));  // open: preset, en, reset
  D_Flip_Flop d_ff_3 (.clk(clock_1_out), .D(in_1), .Q(d_ff_3_q), .Qn(d_ff_3_qn));  // open: preset, en, reset
endmodule

module Secuencia_In (
  input  a,
  input  b,
  input  c,
  input  d,
  output x,
  output y,
  output z
);

  wire and_2_out, and_3_out, and_4_out, not_1_out, not_2_out, not_3_out, not_4_out;

  and and_1 (x, c, d);
  not not_1 (not_1_out, a);
  and and_2 (and_2_out, not_1_out, not_2_out, d);
  not not_2 (not_2_out, c);
  and and_3 (and_3_out, a, c, not_3_out);
  not not_3 (not_3_out, d);
  and and_4 (and_4_out, a, b, not_4_out);
  not not_4 (not_4_out, d);
  or or_1 (y, and_2_out, and_3_out, and_4_out);

  assign z = a;
endmodule

module Secuencia_Out (
  input  a,
  input  b,
  input  c,
  output x
);


  assign x = a;
endmodule
